# Fritzing sketch schematic (saved by Fritzing 0.9.6b)
breadboards: 1

parts:
  U1 = ATTINY13 [package=dip]
  U2 = ATTINY45 [package=dip]  # not connected
  Part1 = NRF24L01+ Breakout Board
  LCD = Grove OLED 128x96
  RHT1 = Humidity and Temperature Sensor RHT03

nets:
  N1: U1.PB3(ADC3), Part1.CS
  N2: U1.PB4(ADC2), RHT1.Data-signal
  GND: U1.GND, Part1.GND, LCD.GND, RHT1.GND_1, RHT1.GND_2
  N3: U1.PB0(MOSI), Part1.MOSI, LCD.SCL
  N4: U1.PB1(MISO), Part1.MISO
  N5: U1.PB2(SCK_ADC1), Part1.SCK, LCD.SDA
  VCC: U1.VCC, Part1.VCC, LCD.VCC, RHT1.Vcc
